# Fritzing sketch project (saved by Fritzing 0.9.3b)
circuit board: 8.77309cm x 6.81729cm

parts:
  U1 = NodeMCU V1.0
  DHT1 = DHT11 Humitidy and Temperature Sensor
  R2 = RELAY [package=relay-jzc]
  R1 = RELAY [package=relay-jzc]
  R4 = RELAY [package=relay-jzc]
  R3 = RELAY [package=relay-jzc]
  LED1 = smd LED [color="White (4500K)" package="1206 [SMD]"]
  LED2 = smd LED [color="White (4500K)" package="1206 [SMD]"]
  Outlet = Camdenboss CTB0158-2 [part_number=CTB0158-2 package=THT]
  Fan = Camdenboss CTB0158-2 [part_number=CTB0158-2 package=THT]
  Main_Power = Camdenboss CTB0158-3 [part_number=CTB0158-3 package=THT]

nets (from the schematic view):
  N1: U1.D1, R1.COIL2
  N2: U1.D2, DHT1.DATA
  N3: U1.D3, R2.COIL2
  3V3: U1.3V3, DHT1.VDD
  GND: U1.GND, DHT1.GND, R2.COIL1, R1.COIL1, R4.COIL1, R3.COIL1
  N4: U1.D5, R3.COIL2
  N5: U1.D7, R4.COIL2
  N6: R2.NC, R1.NC, R4.NO, R3.NO, Main_Power.pin1
  N7: R2.MAIN, LED2.anode
  N8: R1.MAIN, LED1.anode
  N9: R4.MAIN, Outlet.terminal_2
  N10: R3.MAIN, Fan.terminal_2
  N11: LED1.cathode, LED2.cathode, Outlet.terminal_1, Fan.terminal_1, Main_Power.terminal_2

custom parts:
  NodeMCU V1.0: ESP8266 based NodeMCU
  DHT11 Humitidy and Temperature Sensor: DHT11 Humidity and Temperature Sensor
